// Logisim project CPU.circ as structural Verilog: 7 circuits, main circuit Register File
module Main (
  input  [17:0] wData,
  output [17:0] out_2,
  output [17:0] out_3,
  output [17:0] out_4,
  output [17:0] out_5,
  output [17:0] out_6,
  output [17:0] out_7,
  output [17:0] out_8,
  output [17:0] out_9,
  output [17:0] out_10,
  output [3:0] _4_7_Bits,
  output [17:0] out_12,
  output [3:0] _8_11_Bits,
  output [17:0] out_14,
  output [3:0] _12_15_Bits,
  output [17:0] out_16,
  output [17:0] out_17,
  output [17:0] out_18,
  output [17:0] out_19,
  output [17:0] out_20,
  output [17:0] out_21
);

  wire clock_1_out, control_unit_1_p5, control_unit_1_p8, control_unit_1_p9, MemRead;
  wire [1:0] control_unit_1_p7;
  wire [17:0] adder_1_out, multiplexer_1_out, PC_q, ram_1_data, register_file_1_odata2, rom_1_data, undriven;

  Clock clock_1 (.out(clock_1_out));
  Adder_part #(.width(18)) adder_1 (.a(PC_q), .b(18'h1), .out(adder_1_out));  // open: cin, cout
  Register #(.width(18)) PC (.D(adder_1_out), .Q(PC_q), .clk(clock_1_out));  // open: en, clr
  ROM #(.addrWidth(18), .dataWidth(18)) rom_1 (.addr(PC_q), .data(rom_1_data), .sel(1'b1));
  Register_File register_file_1 (
    .rReg1(_4_7_Bits), .rReg2(_8_11_Bits), .wData(wData), .oData1(out_8), .oData2(register_file_1_odata2),
    .R0(out_2), .wReg(_12_15_Bits), .R1(out_3), .R2(out_4), .R3(out_5), .R4(out_6), .R6(out_9), .R7(out_10),
    .R8(out_12), .R10(out_16), .R11(out_17), .R12(out_18), .R13(out_19), .R14(out_20), .R15(out_21),
    .WE(control_unit_1_p9), .Clock(clock_1_out), .R5(out_7), .R9(out_14));
  // Control_Unit control_unit_1: pin names not known; wires that end beside it: rom_1_data, _8_11_Bits, _4_7_Bits, _12_15_Bits, control_unit_1_p5, MemRead, control_unit_1_p7, control_unit_1_p8, control_unit_1_p9
  ALU alu_1 (.input1(undriven), .input2(register_file_1_odata2), .ALUcontrol(control_unit_1_p7));  // open: output
  Multiplexer #(.select(4), .width(18), .enable("false")) multiplexer_1 (
    .in0(out_2), .in1(out_3), .in2(out_4), .in3(out_5), .in4(out_6), .in5(out_7), .in6(out_9), .in7(out_10),
    .in8(out_12), .in9(out_14), .in10(out_16), .in11(out_17), .in12(out_18), .in13(out_19), .in14(out_20),
    .in15(out_21), .out(multiplexer_1_out), .sel(_12_15_Bits));
  Multiplexer #(.width(18), .enable("false")) multiplexer_2 (
    .in0(ram_1_data), .in1(ram_1_data), .sel(MemRead));  // open: out
  RAM #(.addrWidth(10), .dataWidth(18), .bus("separate")) ram_1 (
    .din(multiplexer_1_out), .data(ram_1_data), .str(control_unit_1_p5), .sel(1'b1), .clk(clock_1_out),
    .ld(MemRead), .clr(1'b0));  // open: addr

  // Other names for the same wires on the sheet: R0[17:0] = out_2; R1[17:0] = out_3; R2[17:0] = out_4;
  //   R3[17:0] = out_5; R4[17:0] = out_6; R5[17:0] = out_7; R6[17:0] = out_9; R7[17:0] = out_10; R8[17:0] = out_12;
  //   R9[17:0] = out_14; R10[17:0] = out_16; R11[17:0] = out_17; R12[17:0] = out_18; R13[17:0] = out_19;
  //   R14[17:0] = out_20; R15[17:0] = out_21

  // Notes on the sheet:
  //   contents of rom_1 (hex, n*v repeats v):
  //   1c504
endmodule

module Register_File (
  input  [3:0] rReg1,
  input  [3:0] rReg2,
  input  [17:0] wData,
  input  [3:0] wReg,
  input  WE,
  input  Clock,
  output [17:0] R0,
  output [17:0] R1,
  output [17:0] R2,
  output [17:0] R3,
  output [17:0] oData1,
  output [17:0] R4,
  output [17:0] R5,
  output [17:0] oData2,
  output [17:0] R6,
  output [17:0] R7,
  output [17:0] R8,
  output [17:0] R9,
  output [17:0] R10,
  output [17:0] R11,
  output [17:0] R12,
  output [17:0] R13,
  output [17:0] R14,
  output [17:0] R15
);

  wire and_1_out, and_2_out, and_3_out, and_4_out, and_5_out, and_6_out, and_7_out, and_8_out, and_9_out,
       and_10_out, and_11_out, and_12_out, and_13_out, and_14_out, and_15_out, and_16_out, decoder_1_out0,
       decoder_1_out1, decoder_1_out2, decoder_1_out3, decoder_1_out4, decoder_1_out5, decoder_1_out6,
       decoder_1_out7, decoder_1_out8, decoder_1_out9, decoder_1_out10, decoder_1_out11, decoder_1_out12,
       decoder_1_out13, decoder_1_out14, decoder_1_out15, decoder_2_out0, decoder_2_out1, decoder_2_out2,
       decoder_2_out3, decoder_2_out4, decoder_2_out5, decoder_2_out6, decoder_2_out7, decoder_2_out8,
       decoder_2_out9, decoder_2_out10, decoder_2_out11, decoder_2_out12, decoder_2_out13, decoder_2_out14,
       decoder_2_out15, decoder_3_out0, decoder_3_out1, decoder_3_out2, decoder_3_out3, decoder_3_out4,
       decoder_3_out5, decoder_3_out6, decoder_3_out7, decoder_3_out8, decoder_3_out9, decoder_3_out10,
       decoder_3_out11, decoder_3_out12, decoder_3_out13, decoder_3_out14, decoder_3_out15;

  Decoder #(.select(4), .enable("false")) decoder_1 (
    .out0(decoder_1_out0), .out1(decoder_1_out1), .out2(decoder_1_out2), .out3(decoder_1_out3),
    .out4(decoder_1_out4), .out5(decoder_1_out5), .out6(decoder_1_out6), .out7(decoder_1_out7),
    .out8(decoder_1_out8), .out9(decoder_1_out9), .out10(decoder_1_out10), .out11(decoder_1_out11),
    .out12(decoder_1_out12), .out13(decoder_1_out13), .out14(decoder_1_out14), .out15(decoder_1_out15),
    .sel(rReg1));
  Decoder #(.select(4), .enable("false")) decoder_2 (
    .out0(decoder_2_out0), .out1(decoder_2_out1), .out2(decoder_2_out2), .out3(decoder_2_out3),
    .out4(decoder_2_out4), .out5(decoder_2_out5), .out6(decoder_2_out6), .out7(decoder_2_out7),
    .out8(decoder_2_out8), .out9(decoder_2_out9), .out10(decoder_2_out10), .out11(decoder_2_out11),
    .out12(decoder_2_out12), .out13(decoder_2_out13), .out14(decoder_2_out14), .out15(decoder_2_out15),
    .sel(rReg2));
  Decoder #(.select(4), .enable("false")) decoder_3 (
    .out0(decoder_3_out0), .out1(decoder_3_out1), .out2(decoder_3_out2), .out3(decoder_3_out3),
    .out4(decoder_3_out4), .out5(decoder_3_out5), .out6(decoder_3_out6), .out7(decoder_3_out7),
    .out8(decoder_3_out8), .out9(decoder_3_out9), .out10(decoder_3_out10), .out11(decoder_3_out11),
    .out12(decoder_3_out12), .out13(decoder_3_out13), .out14(decoder_3_out14), .out15(decoder_3_out15),
    .sel(wReg));
  and and_1 (and_1_out, decoder_3_out0, WE);
  and and_2 (and_2_out, decoder_3_out1, WE);
  and and_3 (and_3_out, decoder_3_out2, WE);
  and and_4 (and_4_out, decoder_3_out3, WE);
  and and_5 (and_5_out, decoder_3_out4, WE);
  and and_6 (and_6_out, decoder_3_out5, WE);
  and and_7 (and_7_out, decoder_3_out6, WE);
  and and_8 (and_8_out, decoder_3_out7, WE);
  and and_9 (and_9_out, decoder_3_out8, WE);
  and and_10 (and_10_out, decoder_3_out9, WE);
  and and_11 (and_11_out, decoder_3_out10, WE);
  and and_12 (and_12_out, decoder_3_out11, WE);
  and and_13 (and_13_out, decoder_3_out12, WE);
  and and_14 (and_14_out, decoder_3_out13, WE);
  and and_15 (and_15_out, decoder_3_out14, WE);
  and and_16 (and_16_out, decoder_3_out15, WE);
  Register #(.width(18)) register_1 (.D(wData), .en(and_1_out), .Q(R0), .clk(Clock), .clr(1'b0));
  Register #(.width(18)) register_2 (.D(wData), .en(and_2_out), .Q(R1), .clk(Clock), .clr(1'b0));
  Register #(.width(18)) register_3 (.D(wData), .en(and_3_out), .Q(R2), .clk(Clock), .clr(1'b0));
  Register #(.width(18)) register_4 (.D(wData), .en(and_4_out), .Q(R3), .clk(Clock), .clr(1'b0));
  Register #(.width(18)) register_5 (.D(wData), .en(and_5_out), .Q(R4), .clk(Clock), .clr(1'b0));
  Register #(.width(18)) register_6 (.D(wData), .en(and_6_out), .Q(R5), .clk(Clock), .clr(1'b0));
  Register #(.width(18)) register_7 (.D(wData), .en(and_7_out), .Q(R6), .clk(Clock), .clr(1'b0));
  Register #(.width(18)) register_8 (.D(wData), .en(and_8_out), .Q(R7), .clk(Clock), .clr(1'b0));
  Register #(.width(18)) register_9 (.D(wData), .en(and_9_out), .Q(R8), .clk(Clock), .clr(1'b0));
  Register #(.width(18)) register_10 (.D(wData), .en(and_10_out), .Q(R9), .clk(Clock), .clr(1'b0));
  Register #(.width(18)) register_11 (.D(wData), .en(and_11_out), .Q(R10), .clk(Clock), .clr(1'b0));
  Register #(.width(18)) register_12 (.D(wData), .en(and_12_out), .Q(R11), .clk(Clock), .clr(1'b0));
  Register #(.width(18)) register_13 (.D(wData), .en(and_13_out), .Q(R12), .clk(Clock), .clr(1'b0));
  Register #(.width(18)) register_14 (.D(wData), .en(and_14_out), .Q(R13), .clk(Clock), .clr(1'b0));
  Register #(.width(18)) register_15 (.D(wData), .en(and_15_out), .Q(R14), .clk(Clock), .clr(1'b0));
  Register #(.width(18)) register_16 (.D(wData), .en(and_16_out), .Q(R15), .clk(Clock), .clr(1'b0));
  assign oData1 = decoder_1_out0 ? R0 : 18'bz;  // Controlled_Buffer controlled_buffer_1
  assign oData2 = decoder_2_out0 ? R0 : 18'bz;  // Controlled_Buffer controlled_buffer_2
  assign oData1 = decoder_1_out1 ? R1 : 18'bz;  // Controlled_Buffer controlled_buffer_3
  assign oData2 = decoder_2_out1 ? R1 : 18'bz;  // Controlled_Buffer controlled_buffer_4
  assign oData1 = decoder_1_out2 ? R2 : 18'bz;  // Controlled_Buffer controlled_buffer_5
  assign oData2 = decoder_2_out2 ? R2 : 18'bz;  // Controlled_Buffer controlled_buffer_6
  assign oData1 = decoder_1_out3 ? R3 : 18'bz;  // Controlled_Buffer controlled_buffer_7
  assign oData2 = decoder_2_out3 ? R3 : 18'bz;  // Controlled_Buffer controlled_buffer_8
  assign oData1 = decoder_1_out4 ? R4 : 18'bz;  // Controlled_Buffer controlled_buffer_9
  assign oData2 = decoder_2_out4 ? R4 : 18'bz;  // Controlled_Buffer controlled_buffer_10
  assign oData1 = decoder_1_out5 ? R5 : 18'bz;  // Controlled_Buffer controlled_buffer_11
  assign oData2 = decoder_2_out5 ? R5 : 18'bz;  // Controlled_Buffer controlled_buffer_12
  assign oData1 = decoder_1_out6 ? R6 : 18'bz;  // Controlled_Buffer controlled_buffer_13
  assign oData2 = decoder_2_out6 ? R6 : 18'bz;  // Controlled_Buffer controlled_buffer_14
  assign oData1 = decoder_1_out7 ? R7 : 18'bz;  // Controlled_Buffer controlled_buffer_15
  assign oData2 = decoder_2_out7 ? R7 : 18'bz;  // Controlled_Buffer controlled_buffer_16
  assign oData1 = decoder_1_out8 ? R8 : 18'bz;  // Controlled_Buffer controlled_buffer_17
  assign oData2 = decoder_2_out8 ? R8 : 18'bz;  // Controlled_Buffer controlled_buffer_18
  assign oData1 = decoder_1_out9 ? R9 : 18'bz;  // Controlled_Buffer controlled_buffer_19
  assign oData2 = decoder_2_out9 ? R9 : 18'bz;  // Controlled_Buffer controlled_buffer_20
  assign oData1 = decoder_1_out10 ? R10 : 18'bz;  // Controlled_Buffer controlled_buffer_21
  assign oData2 = decoder_2_out10 ? R10 : 18'bz;  // Controlled_Buffer controlled_buffer_22
  assign oData1 = decoder_1_out11 ? R11 : 18'bz;  // Controlled_Buffer controlled_buffer_23
  assign oData2 = decoder_2_out11 ? R11 : 18'bz;  // Controlled_Buffer controlled_buffer_24
  assign oData1 = decoder_1_out12 ? R12 : 18'bz;  // Controlled_Buffer controlled_buffer_25
  assign oData2 = decoder_2_out12 ? R12 : 18'bz;  // Controlled_Buffer controlled_buffer_26
  assign oData1 = decoder_1_out13 ? R13 : 18'bz;  // Controlled_Buffer controlled_buffer_27
  assign oData2 = decoder_2_out13 ? R13 : 18'bz;  // Controlled_Buffer controlled_buffer_28
  assign oData1 = decoder_1_out14 ? R14 : 18'bz;  // Controlled_Buffer controlled_buffer_29
  assign oData2 = decoder_2_out14 ? R14 : 18'bz;  // Controlled_Buffer controlled_buffer_30
  assign oData1 = decoder_1_out15 ? R15 : 18'bz;  // Controlled_Buffer controlled_buffer_31
  assign oData2 = decoder_2_out15 ? R15 : 18'bz;  // Controlled_Buffer controlled_buffer_32
endmodule

module Control_Unit (
  input  [17:0] \input ,
  output MemRead,
  output MemWrite,
  output Write_Enable,
  output [1:0] Alu_Input,
  output [13:0] Jump_Adress,
  output [3:0] _7_4_Bits,
  output [3:0] _11_8_Bits,
  output [3:0] _15_12_Bits,
  output [5:0] Imm_Value
);

  wire decoder_1_out0, decoder_1_out1, decoder_1_out2, decoder_1_out3, decoder_1_out4, decoder_1_out5,
       decoder_1_out6, decoder_1_out7, decoder_1_out8, decoder_1_out9, decoder_1_out10, decoder_1_out11,
       decoder_1_out12, decoder_1_out14, Imm, or_1_out;

  Decoder #(.select(4)) decoder_1 (
    .out0(decoder_1_out0), .out1(decoder_1_out1), .out2(decoder_1_out2), .out3(decoder_1_out3),
    .out4(decoder_1_out4), .out5(decoder_1_out5), .out6(decoder_1_out6), .out7(decoder_1_out7),
    .out8(decoder_1_out8), .out9(decoder_1_out9), .out10(decoder_1_out10), .out11(decoder_1_out11),
    .out12(decoder_1_out12), .out13(MemRead), .out14(decoder_1_out14), .out15(MemWrite), .sel(\input [3:0]));  // open: en
  Priority_Encoder #(.select(2)) priority_encoder_1 (
    .in0(decoder_1_out4), .in1(decoder_1_out5), .in2(decoder_1_out6), .in3(decoder_1_out7), .out(Alu_Input));  // open: gs, en_out, en_in
  Priority_Encoder #(.select(2)) priority_encoder_2 (
    .in0(decoder_1_out0), .in1(decoder_1_out1), .in2(decoder_1_out2), .in3(decoder_1_out3), .out(Alu_Input));  // open: gs, en_out, en_in
  or or_1 (or_1_out, decoder_1_out0, decoder_1_out1, decoder_1_out2, decoder_1_out3);
  or or_2 (Write_Enable, or_1_out, MemRead, Imm);

  assign _7_4_Bits = \input [7:4];
  assign _11_8_Bits = \input [11:8];
  assign _15_12_Bits = \input [15:12];
  assign Imm_Value = \input [17:12];
  assign Jump_Adress = \input [17:4];

  // Other names for the same wires on the sheet: WriteEnable = Write_Enable

  // Notes on the sheet:
  //   ADD
  //   AND
  //   ST
  //   OR
  //   XOR
  //   ADDI
  //   ANDI
  //   ORI
  //   XORI
  //   JUMP
  //   BGT
  //   BEQ
  //   BGE
  //   BLT
  //   LD
  //   BLE
endmodule

module ALU (
  input  [1:0] ALUcontrol,
  input  [17:0] input1,
  input  [17:0] input2,
  output [17:0] \output 
);

  wire decoder_1_out0, decoder_1_out1, decoder_1_out2, decoder_1_out3;
  wire [17:0] adder_1_output, and_1_out, or_1_out, xor_1_out;

  Decoder #(.select(2)) decoder_1 (
    .out0(decoder_1_out0), .out1(decoder_1_out1), .out2(decoder_1_out2), .out3(decoder_1_out3),
    .sel(ALUcontrol));  // open: en
  Adder adder_1 (.\output (adder_1_output), .input2(input2), .input1(input1));
  assign and_1_out = input1 & input2;  // AND_Gate and_1, 18 bits wide
  assign or_1_out = input1 | input2;  // OR_Gate or_1, 18 bits wide
  assign xor_1_out = input1 ^ input2;  // XOR_Gate xor_1, 18 bits wide
  assign \output  = decoder_1_out0 ? adder_1_output : 18'bz;  // Controlled_Buffer controlled_buffer_1
  assign \output  = decoder_1_out1 ? and_1_out : 18'bz;  // Controlled_Buffer controlled_buffer_2
  assign \output  = decoder_1_out2 ? or_1_out : 18'bz;  // Controlled_Buffer controlled_buffer_3
  assign \output  = decoder_1_out3 ? xor_1_out : 18'bz;  // Controlled_Buffer controlled_buffer_4

  // Notes on the sheet:
  //   0 - ADD
  //   1 - AND
  //   2 - OR
  //   3 - XOR
endmodule

module Adder (
  input  [17:0] input2,
  input  [17:0] input1,
  output [17:0] \output 
);

  wire full_adder_1_c_out, full_adder_2_c_out, full_adder_3_c_out, full_adder_4_c_out, full_adder_5_c_out,
       full_adder_6_c_out, full_adder_7_c_out, full_adder_8_c_out, full_adder_9_c_out, full_adder_10_c_out,
       full_adder_11_c_out, full_adder_12_c_out, full_adder_13_c_out, full_adder_14_c_out,
       full_adder_15_c_out, full_adder_16_c_out, half_adder_1_cout;

  Half_Adder half_adder_1 (.a(input1[0]), .b(input2[0]), .sum(\output [0]), .Cout(half_adder_1_cout));
  Full_Adder full_adder_1 (
    .a(input1[1]), .b(input2[1]), .C_in(half_adder_1_cout), .sum(\output [1]), .C_out(full_adder_1_c_out));
  Full_Adder full_adder_2 (
    .a(input1[2]), .b(input2[2]), .C_in(full_adder_1_c_out), .sum(\output [2]), .C_out(full_adder_2_c_out));
  Full_Adder full_adder_3 (
    .a(input1[3]), .b(input2[3]), .C_in(full_adder_2_c_out), .sum(\output [3]), .C_out(full_adder_3_c_out));
  Full_Adder full_adder_4 (
    .a(input1[4]), .b(input2[4]), .C_in(full_adder_3_c_out), .sum(\output [4]), .C_out(full_adder_4_c_out));
  Full_Adder full_adder_5 (
    .a(input1[5]), .b(input2[5]), .C_in(full_adder_4_c_out), .sum(\output [5]), .C_out(full_adder_5_c_out));
  Full_Adder full_adder_6 (
    .a(input1[6]), .b(input2[6]), .C_in(full_adder_5_c_out), .sum(\output [6]), .C_out(full_adder_6_c_out));
  Full_Adder full_adder_7 (
    .a(input1[7]), .b(input2[7]), .C_in(full_adder_6_c_out), .sum(\output [7]), .C_out(full_adder_7_c_out));
  Full_Adder full_adder_8 (
    .a(input1[8]), .b(input2[8]), .C_in(full_adder_7_c_out), .sum(\output [8]), .C_out(full_adder_8_c_out));
  Full_Adder full_adder_9 (
    .a(input1[9]), .b(input2[9]), .C_in(full_adder_8_c_out), .sum(\output [9]), .C_out(full_adder_9_c_out));
  Full_Adder full_adder_10 (
    .a(input1[10]), .b(input2[10]), .C_in(full_adder_9_c_out), .sum(\output [10]), .C_out(full_adder_10_c_out));
  Full_Adder full_adder_11 (
    .a(input1[11]), .b(input2[11]), .C_in(full_adder_10_c_out), .sum(\output [11]),
    .C_out(full_adder_11_c_out));
  Full_Adder full_adder_12 (
    .a(input1[12]), .b(input2[12]), .C_in(full_adder_11_c_out), .sum(\output [12]),
    .C_out(full_adder_12_c_out));
  Full_Adder full_adder_13 (
    .a(input1[13]), .b(input2[13]), .C_in(full_adder_12_c_out), .sum(\output [13]),
    .C_out(full_adder_13_c_out));
  Full_Adder full_adder_14 (
    .a(input1[14]), .b(input2[14]), .C_in(full_adder_13_c_out), .sum(\output [14]),
    .C_out(full_adder_14_c_out));
  Full_Adder full_adder_15 (
    .a(input1[15]), .b(input2[15]), .C_in(full_adder_14_c_out), .sum(\output [15]),
    .C_out(full_adder_15_c_out));
  Full_Adder full_adder_16 (
    .a(input1[16]), .b(input2[16]), .C_in(full_adder_15_c_out), .sum(\output [16]),
    .C_out(full_adder_16_c_out));
  Full_Adder full_adder_17 (
    .a(input1[17]), .b(input2[17]), .C_in(full_adder_16_c_out), .sum(\output [17]));  // open: C_out
endmodule

module Half_Adder (
  input  a,
  input  b,
  output sum,
  output Cout
);

  xor xor_1 (sum, a, b);
  and and_1 (Cout, a, b);
endmodule

module Full_Adder (
  input  a,
  input  b,
  input  C_in,
  output sum,
  output C_out
);

  wire and_1_out, and_2_out, or_1_out;

  xor xor_1 (sum, a, b, C_in);
  and and_1 (and_1_out, ~C_in, a, b);  // AND_Gate
  or or_1 (or_1_out, b, a);
  and and_2 (and_2_out, C_in, or_1_out);
  or or_2 (C_out, and_1_out, and_2_out);
endmodule
