// Logisim project logisimBird.circ as structural Verilog: 14 circuits, main circuit main
// Main Circuit
module main (
  input  CLK,
  output [3:0] DISP_3_0,
  output [3:0] DISP_7_4,
  output [3:0] DISP_11_8,
  output [3:0] DISP_15_12
);

  wire MEMWT;
  wire [11:0] Addres_Out_11_0;
  wire [15:0] Data_Out_15_0, DIN;

  Output output_1 (.DATA_OUT(Data_Out_15_0), .REG({DISP_15_12, DISP_11_8, DISP_7_4, DISP_3_0}), .LOAD(1'b1), .CLK(CLK));
  CPU cpu_1 (.ADDRES_OUT(Addres_Out_11_0), .MEMLD(MEMWT), .DATA_OUT(Data_Out_15_0), .in_2(CLK), .DIN(DIN));
  RAM #(.addrWidth(12), .dataWidth(16), .bus("separate")) ram_1 (
    .addr(Addres_Out_11_0), .din(Data_Out_15_0), .data(DIN), .str(MEMWT), .clk(CLK));  // open: sel, ld, clr

  // Other names for the same wires on the sheet: CLOCK = CLK
endmodule

module ALU (
  input  [15:0] SRCL,
  input  [15:0] SRCR,
  input  [5:0] ALUSELECT,
  input  CLOCK,
  input  ZFLD,
  output [15:0] ALUOUT,
  output ZF
);

  wire not_2_out, not_3_out, not_4_out, not_5_out, not_6_out, not_7_out, not_8_out, not_9_out, not_10_out,
       not_11_out, not_12_out, not_13_out, not_14_out, not_15_out, not_16_out, not_17_out, ZF_out;
  wire [15:0] adder_1_out, adder_2_out, and_1_out, multiplexer_1_out, not_1_out, or_1_out, subtractor_1_out,
       subtractor_2_out, xor_1_out;

  // Probe on nothing
  Adder #(.width(16)) adder_1 (.a(SRCR), .b(SRCL), .out(adder_1_out));  // open: cin, cout
  Subtractor #(.width(16)) subtractor_1 (.a(SRCR), .b(SRCL), .out(subtractor_1_out));  // open: bin, bout
  assign and_1_out = SRCR & SRCL;  // AND_Gate and_1, 16 bits wide
  assign or_1_out = SRCR | SRCL;  // OR_Gate or_1, 16 bits wide
  assign xor_1_out = SRCR ^ SRCL;  // XOR_Gate xor_1, 16 bits wide
  assign not_1_out = ~SRCR;  // NOT_Gate not_1, 16 bits wide
  Adder #(.width(16)) adder_2 (.a(SRCR), .b(16'h1), .out(adder_2_out));  // open: cin, cout
  Subtractor #(.width(16)) subtractor_2 (.a(SRCR), .b(16'h1), .out(subtractor_2_out));  // open: bin, bout
  Multiplexer #(.select(3), .width(16), .enable("false")) multiplexer_1 (
    .in0(not_1_out), .in1(SRCR), .in2(adder_2_out), .in3(subtractor_2_out), .out(multiplexer_1_out),
    .sel(ALUSELECT[2:0]));  // open: in4, in5, in6, in7
  Multiplexer #(.select(3), .width(16), .enable("false")) multiplexer_2 (
    .in0(adder_1_out), .in1(subtractor_1_out), .in2(and_1_out), .in3(or_1_out), .in4(xor_1_out),
    .in7(multiplexer_1_out), .out(ALUOUT), .sel(ALUSELECT[5:3]));  // open: in5, in6
  not not_2 (not_2_out, ALUOUT[14]);
  not not_3 (not_3_out, ALUOUT[15]);
  not not_4 (not_4_out, ALUOUT[11]);
  not not_5 (not_5_out, ALUOUT[10]);
  not not_6 (not_6_out, ALUOUT[13]);
  not not_7 (not_7_out, ALUOUT[12]);
  not not_8 (not_8_out, ALUOUT[7]);
  not not_9 (not_9_out, ALUOUT[9]);
  not not_10 (not_10_out, ALUOUT[6]);
  not not_11 (not_11_out, ALUOUT[8]);
  and u_ZF (ZF_out, not_3_out, not_2_out, not_6_out, not_7_out, not_4_out, not_5_out, not_9_out, not_11_out, not_8_out, not_10_out, not_13_out, not_12_out, not_14_out, not_15_out, not_17_out, not_16_out);
  _1_bit_Register u_1_bit_register_1 (.DATA(ZF_out), .OUT(ZF), .LOAD(ZFLD), .CLK(CLOCK));
  not not_12 (not_12_out, ALUOUT[4]);
  not not_13 (not_13_out, ALUOUT[5]);
  not not_14 (not_14_out, ALUOUT[3]);
  not not_15 (not_15_out, ALUOUT[2]);
  not not_16 (not_16_out, ALUOUT[0]);
  not not_17 (not_17_out, ALUOUT[1]);
endmodule

module _1_bit_Register (
  input  DATA,
  input  LOAD,
  input  CLK,
  output OUT
);

  wire and_1_out, and_2_out, not_1_out;

  not not_1 (not_1_out, DATA);
  and and_1 (and_1_out, DATA, LOAD);
  and and_2 (and_2_out, not_1_out, LOAD);
  S_R_Flip_Flop s_r_ff_1 (.S(and_1_out), .clk(CLK), .R(and_2_out), .Q(OUT));  // open: Qn, preset, reset, en
endmodule

module REGBANK (
  input  [15:0] DOUT,
  input  [2:0] REGSE,
  input  REGLD,
  input  INC,
  input  DEC,
  input  CLK,
  output [15:0] REG0,
  output [15:0] REG1,
  output [15:0] REG2,
  output [15:0] REG3,
  output [15:0] REG4,
  output [15:0] REG5,
  output [15:0] REG6,
  output [15:0] REG7
);

  wire and_1_out, and_2_out, and_3_out, and_4_out, and_5_out, and_6_out, and_7_out, and_8_out,
       decoder_1_out0, decoder_1_out1, decoder_1_out2, decoder_1_out3, decoder_1_out4, decoder_1_out5,
       decoder_1_out6, decoder_1_out7;

  Decoder #(.select(3), .enable("false")) decoder_1 (
    .out0(decoder_1_out0), .out1(decoder_1_out1), .out2(decoder_1_out2), .out3(decoder_1_out3),
    .out4(decoder_1_out4), .out5(decoder_1_out5), .out6(decoder_1_out6), .out7(decoder_1_out7), .sel(REGSE));
  and and_1 (and_1_out, decoder_1_out0, REGLD);
  and and_2 (and_2_out, decoder_1_out1, REGLD);
  and and_3 (and_3_out, decoder_1_out2, REGLD);
  and and_4 (and_4_out, decoder_1_out3, REGLD);
  and and_5 (and_5_out, decoder_1_out4, REGLD);
  and and_6 (and_6_out, decoder_1_out5, REGLD);
  and and_7 (and_7_out, decoder_1_out6, REGLD);
  and and_8 (and_8_out, decoder_1_out7, REGLD);
  _16_bit_Register u_16_bit_register_1 (.DATA(DOUT), .LOAD(and_1_out), .CLK(CLK), .OUT(REG0));
  _16_bit_Register u_16_bit_register_2 (.DATA(DOUT), .LOAD(and_2_out), .CLK(CLK), .OUT(REG1));
  _16_bit_Register u_16_bit_register_3 (.DATA(DOUT), .LOAD(and_3_out), .CLK(CLK), .OUT(REG2));
  _16_bit_Register u_16_bit_register_4 (.DATA(DOUT), .LOAD(and_4_out), .CLK(CLK), .OUT(REG3));
  _16_bit_Register u_16_bit_register_5 (.DATA(DOUT), .LOAD(and_5_out), .CLK(CLK), .OUT(REG4));
  _16_bit_Register u_16_bit_register_6 (.DATA(DOUT), .LOAD(and_6_out), .CLK(CLK), .OUT(REG5));
  _16_bit_Register u_16_bit_register_7 (.DATA(DOUT), .LOAD(and_7_out), .CLK(CLK), .OUT(REG6));
  SP_Register sp_register_1 (.DataIn(DOUT), .INC(INC), .DEC(DEC), .LOAD(and_8_out), .CLOCK(CLK), .DataOut(REG7));
endmodule

module _4_bit_Register (
  input  [3:0] DATA,
  input  LOAD,
  input  CLK,
  output [3:0] OUT
);

  wire and_1_out, and_2_out, and_3_out, and_4_out, and_5_out, and_6_out, and_7_out, and_8_out, not_1_out,
       not_2_out, not_3_out, not_4_out;

  not not_1 (not_1_out, DATA[0]);
  not not_2 (not_2_out, DATA[1]);
  not not_3 (not_3_out, DATA[2]);
  not not_4 (not_4_out, DATA[3]);
  and and_1 (and_1_out, DATA[0], LOAD);
  and and_2 (and_2_out, not_1_out, LOAD);
  and and_3 (and_3_out, DATA[1], LOAD);
  and and_4 (and_4_out, not_2_out, LOAD);
  and and_5 (and_5_out, DATA[2], LOAD);
  and and_6 (and_6_out, not_3_out, LOAD);
  and and_7 (and_7_out, DATA[3], LOAD);
  and and_8 (and_8_out, not_4_out, LOAD);
  S_R_Flip_Flop s_r_ff_1 (.S(and_1_out), .clk(CLK), .R(and_2_out), .Q(OUT[0]));  // open: Qn, preset, reset, en
  S_R_Flip_Flop s_r_ff_2 (.S(and_3_out), .clk(CLK), .R(and_4_out), .Q(OUT[1]));  // open: Qn, preset, reset, en
  S_R_Flip_Flop s_r_ff_3 (.S(and_5_out), .clk(CLK), .R(and_6_out), .Q(OUT[2]));  // open: Qn, preset, reset, en
  S_R_Flip_Flop s_r_ff_4 (.S(and_7_out), .clk(CLK), .R(and_8_out), .Q(OUT[3]));  // open: Qn, preset, reset, en
endmodule

module _16_bit_Register (
  input  [15:0] DATA,
  input  LOAD,
  input  CLK,
  output [15:0] OUT
);

  _4_bit_Register u_4_bit_register_1 (.DATA(DATA[3:0]), .LOAD(LOAD), .CLK(CLK), .OUT(OUT[3:0]));
  _4_bit_Register u_4_bit_register_2 (.DATA(DATA[7:4]), .LOAD(LOAD), .CLK(CLK), .OUT(OUT[7:4]));
  _4_bit_Register u_4_bit_register_3 (.DATA(DATA[11:8]), .LOAD(LOAD), .CLK(CLK), .OUT(OUT[11:8]));
  _4_bit_Register u_4_bit_register_4 (.DATA(DATA[15:12]), .LOAD(LOAD), .CLK(CLK), .OUT(OUT[15:12]));
endmodule

// SP Reg
module SP_Register (
  input  [15:0] DataIn,
  input  INC,
  input  DEC,
  input  LOAD,
  input  CLOCK,
  output [15:0] DataOut
);

  wire or_1_out;
  wire [15:0] adder_1_out, multiplexer_1_out, subtractor_1_out;

  or or_1 (or_1_out, DEC, INC, LOAD);
  Multiplexer #(.select(2), .width(16), .enable("false")) multiplexer_1 (
    .in0(DataIn), .in1(subtractor_1_out), .in2(adder_1_out), .out(multiplexer_1_out), .sel({INC, DEC}));  // open: in3
  _16_bit_Register u_16_bit_register_1 (.DATA(multiplexer_1_out), .LOAD(or_1_out), .CLK(CLOCK), .OUT(DataOut));
  Adder #(.width(16)) adder_1 (.a(DataOut), .b(16'h1), .out(adder_1_out));  // open: cin, cout
  Subtractor #(.width(16)) subtractor_1 (.a(DataOut), .b(16'h1), .out(subtractor_1_out));  // open: bin, bout
endmodule

module _12_bit_Register (
  input  [11:0] DATA,
  input  LOAD,
  input  CLK,
  output [11:0] out_4
);

  _4_bit_Register u_4_bit_register_1 (.DATA(DATA[3:0]), .LOAD(LOAD), .CLK(CLK), .OUT(out_4[3:0]));
  _4_bit_Register u_4_bit_register_2 (.DATA(DATA[7:4]), .LOAD(LOAD), .CLK(CLK), .OUT(out_4[7:4]));
  _4_bit_Register u_4_bit_register_3 (.DATA(DATA[11:8]), .LOAD(LOAD), .CLK(CLK), .OUT(out_4[11:8]));
endmodule

module PC (
  input  [11:0] ADDRESS_IN,
  input  PCLOAD,
  input  PCINC,
  input  CLK,
  output [11:0] ADDRESS_OUT
);

  wire or_1_out;
  wire [11:0] adder_1_out, multiplexer_1_out;

  Adder #(.width(12)) adder_1 (.a(ADDRESS_OUT), .b(12'h1), .out(adder_1_out));  // open: cin, cout
  Multiplexer #(.width(12), .enable("false")) multiplexer_1 (
    .in0(adder_1_out), .in1(ADDRESS_IN), .out(multiplexer_1_out), .sel(PCLOAD));
  or or_1 (or_1_out, PCLOAD, PCINC);
  _12_bit_Register u_12_bit_register_1 (.DATA(multiplexer_1_out), .LOAD(or_1_out), .CLK(CLK), .out_4(ADDRESS_OUT));
endmodule

// IR
module Instruction_Register (
  input  [11:0] DIN,
  input  IRLD,
  input  CLOCK,
  output [11:0] Insturction_Register,
  output [2:0] REGSELECT,
  output [2:0] SRC_Right,
  output [2:0] SRC_Left,
  output [5:0] ALUOP
);

  _12_bit_Register u_12_bit_register_1 (
    .DATA(DIN), .LOAD(IRLD), .CLK(CLOCK), .out_4({ALUOP, Insturction_Register[5:0]}));

  assign Insturction_Register[11:6] = ALUOP;
  assign REGSELECT = Insturction_Register[2:0];
  assign SRC_Left = ALUOP[2:0];
  assign SRC_Right = Insturction_Register[5:3];
endmodule

// CONTROL UNIT
module Control_Unit (
  input  [3:0] OPCODE,
  input  ZF,
  input  CLOCK,
  output PCMUX,
  output PCINC,
  output PCLOAD,
  output IRLD,
  output MUX,
  output ZFLD,
  output REGLD,
  output SPDEC,
  output SPINC,
  output MEMLD,
  output DATAMUX,
  output [1:0] ARMUX
);

  wire not_1_out, not_2_out, not_3_out;
  wire [1:1] and_1_out;
  wire [3:0] multiplexer_1_out, multiplexer_2_out, n4_bit_register_1_out, rom_1_data;
  wire [17:17] rom_1_data_2;

  not not_1 (not_1_out, OPCODE[0]);
  not not_2 (not_2_out, OPCODE[1]);
  and and_1 (and_1_out[1], not_1_out, not_2_out, OPCODE[2], not_3_out);
  not not_3 (not_3_out, OPCODE[3]);
  Multiplexer #(.select(2), .width(4), .enable("false")) multiplexer_1 (
    .in0(OPCODE), .in1(OPCODE), .in2(4'b0000), .in3(4'b0101), .out(multiplexer_1_out),
    .sel({and_1_out[1], ZF}));
  Multiplexer #(.width(4), .enable("false")) multiplexer_2 (
    .in0(rom_1_data), .in1(multiplexer_1_out), .out(multiplexer_2_out), .sel(rom_1_data_2[17]));
  _4_bit_Register u_4_bit_register_1 (.DATA(multiplexer_2_out), .LOAD(1'b1), .CLK(CLOCK), .OUT(n4_bit_register_1_out));
  ROM #(.addrWidth(4), .dataWidth(18)) rom_1 (
    .addr(n4_bit_register_1_out),
    .data({rom_1_data_2[17], ARMUX, DATAMUX, MEMLD, SPINC, SPDEC, REGLD, ZFLD, MUX, IRLD, PCLOAD, PCINC, PCMUX, rom_1_data}));  // open: sel

  // Notes on the sheet:
  //   contents of rom_1 (hex, n*v repeats v):
  //   200a0 520 8500 a000 0 40 0 600 12800 100c 16840 100d 10500 10050
endmodule

module CPU (
  input  [15:0] DIN,
  input  in_2,
  output [11:0] ADDRES_OUT,
  output MEMLD,
  output [15:0] DATA_OUT
);

  wire DATAMUX, IRLD, MUX, PCINC, PCLOAD, PCMUX, REGLD, SP_minus_minus, SP_plus_plus, ZF, ZFLD;
  wire [1:0] ARMUX;
  wire [2:0] REGSE, SRCL, SRCR;
  wire [5:0] ALUOP;
  wire [11:0] adder_1_out, bit_extender_1_out, bit_extender_2_out, IR, multiplexer_1_out, PC_ADDR;
  wire [15:0] ALUOUT, bit_extender_3_out, DOUT, multiplexer_2_out, REG_ADDR, regbank_1_reg1, regbank_1_reg2,
       regbank_1_reg3, regbank_1_reg4, regbank_1_reg5, regbank_1_reg6, REGISTER0, SP;

  Multiplexer #(.width(12), .enable("false")) multiplexer_1 (
    .in0(adder_1_out), .in1(DIN[11:0]), .out(multiplexer_1_out), .sel(PCMUX));
  Adder #(.width(12)) adder_1 (.a(PC_ADDR), .b(IR), .out(adder_1_out));  // open: cin, cout
  PC pc_1 (.ADDRESS_IN(multiplexer_1_out), .ADDRESS_OUT(PC_ADDR), .PCLOAD(PCLOAD), .PCINC(PCINC), .CLK(in_2));
  Instruction_Register instruction_register_1 (
    .DIN(DIN[11:0]), .Insturction_Register(IR), .REGSELECT(REGSE), .SRC_Right(SRCR), .SRC_Left(SRCL),
    .ALUOP(ALUOP), .IRLD(IRLD), .CLOCK(in_2));
  Control_Unit control_unit_1 (
    .ZF(ZF), .CLOCK(in_2), .PCMUX(PCMUX), .PCINC(PCINC), .PCLOAD(PCLOAD), .IRLD(IRLD), .MUX(MUX),
    .ZFLD(ZFLD), .REGLD(REGLD), .SPDEC(SP_minus_minus), .SPINC(SP_plus_plus), .MEMLD(MEMLD),
    .DATAMUX(DATAMUX), .ARMUX(ARMUX), .OPCODE(DIN[15:12]));
  Multiplexer #(.width(16), .enable("false")) multiplexer_2 (
    .in0(ALUOUT), .in1(DIN), .out(multiplexer_2_out), .sel(MUX));
  Bit_Extender #(.in_width(16), .out_width(12)) bit_extender_1 (.in(REG_ADDR), .out(bit_extender_1_out));
  Bit_Extender #(.in_width(16), .out_width(12)) bit_extender_2 (.in(SP), .out(bit_extender_2_out));
  REGBANK regbank_1 (
    .DOUT(multiplexer_2_out), .REG0(REGISTER0), .REG1(regbank_1_reg1), .REG2(regbank_1_reg2),
    .REG3(regbank_1_reg3), .REG4(regbank_1_reg4), .REG5(regbank_1_reg5), .REG6(regbank_1_reg6), .REG7(SP),
    .REGSE(REGSE), .REGLD(REGLD), .INC(SP_plus_plus), .DEC(SP_minus_minus), .CLK(in_2));
  Multiplexer #(.select(2), .width(12), .enable("false")) multiplexer_3 (
    .in0(PC_ADDR), .in1(bit_extender_1_out), .in2(bit_extender_2_out), .out(ADDRES_OUT), .sel(ARMUX));  // open: in3
  Multiplexer #(.select(3), .width(16), .enable("false")) multiplexer_4 (
    .in0(REGISTER0), .in1(regbank_1_reg1), .in2(regbank_1_reg2), .in3(regbank_1_reg3), .in4(regbank_1_reg4),
    .in5(regbank_1_reg5), .in6(regbank_1_reg6), .in7(SP), .out(DOUT), .sel(SRCL));
  Multiplexer #(.width(16), .enable("false")) multiplexer_5 (
    .in0(REGISTER0), .in1(bit_extender_3_out), .out(DATA_OUT), .sel(DATAMUX));
  assign bit_extender_3_out = {{4{1'b0}}, PC_ADDR};  // Bit_Extender bit_extender_3
  Multiplexer #(.select(3), .width(16), .enable("false")) multiplexer_6 (
    .in0(REGISTER0), .in1(regbank_1_reg1), .in2(regbank_1_reg2), .in3(regbank_1_reg3), .in4(regbank_1_reg4),
    .in5(regbank_1_reg5), .in6(regbank_1_reg6), .in7(SP), .out(REG_ADDR), .sel(SRCR));
  ALU alu_1 (.ALUSELECT(ALUOP), .CLOCK(in_2), .ZF(ZF), .ALUOUT(ALUOUT), .ZFLD(ZFLD), .SRCL(DOUT), .SRCR(REG_ADDR));

  // Other names for the same wires on the sheet: CLK = in_2; D_11_0[11:0] = DIN[11:0]; OPCODE[3:0] = DIN[15:12]
endmodule

// Output7seg
module Output (
  input  [15:0] DATA_OUT,
  input  LOAD,
  input  CLK,
  output [15:0] REG
);

  _16_bit_Register u_16_bit_register_1 (.DATA(DATA_OUT), .LOAD(LOAD), .CLK(CLK), .OUT(REG));
endmodule

module Top (
);

  wire clock_1_out;
  wire [3:0] main_1_disp_3_0, main_1_disp_7_4, main_1_disp_11_8, main_1_disp_15_12;

  Clock clock_1 (.out(clock_1_out));
  main main_1 (
    .CLK(clock_1_out), .DISP_3_0(main_1_disp_3_0), .DISP_7_4(main_1_disp_7_4), .DISP_11_8(main_1_disp_11_8),
    .DISP_15_12(main_1_disp_15_12));
  Hex_Digit_Display hex_digit_display_1 (.value(main_1_disp_15_12));  // open: dp
  Hex_Digit_Display hex_digit_display_2 (.value(main_1_disp_11_8));  // open: dp
  Hex_Digit_Display hex_digit_display_3 (.value(main_1_disp_7_4));  // open: dp
  Hex_Digit_Display hex_digit_display_4 (.value(main_1_disp_3_0));  // open: dp
endmodule
